// Logisim project 2.circ as structural Verilog: 1 circuit, main circuit minterm
module minterm (
  input  [3:0] fourbitinput,
  output h
);

  wire not_1_out;

  not not_1 (not_1_out, fourbitinput[0]);
  and and_1 (h, not_1_out, fourbitinput[1], fourbitinput[2], fourbitinput[3]);

  // Other names for the same wires on the sheet: A[3:0] = fourbitinput; a_t = fourbitinput[0]; b_t = fourbitinput[1];
  //   c = fourbitinput[2]; d = fourbitinput[3]; B = h
endmodule
