// Logisim project 3.circ as structural Verilog: 1 circuit, main circuit maxterm
module maxterm (
  input  [3:0] fourbitinput,
  output j
);

  wire not_1_out, not_2_out;

  not not_1 (not_1_out, fourbitinput[1]);
  not not_2 (not_2_out, fourbitinput[2]);
  or or_1 (j, fourbitinput[0], not_1_out, not_2_out, fourbitinput[3]);

  // Other names for the same wires on the sheet: a = fourbitinput[0]; I[3:0] = fourbitinput; b = fourbitinput[1];
  //   c = fourbitinput[2]; d = fourbitinput[3]; O = j
endmodule
