// Logisim project 5.circ as structural Verilog: 1 circuit, main circuit singledigit
module singledigit (
  input  [3:0] i,
  output a,
  output b,
  output c,
  output d,
  output e,
  output f,
  output g
);

  wire and_1_out, and_2_out, and_3_out, and_4_out, and_5_out, and_6_out, and_7_out, and_8_out, and_9_out,
       and_10_out, and_11_out, and_12_out, and_13_out, and_14_out, and_15_out, and_16_out, not_1_out,
       not_2_out, not_3_out, not_4_out, not_5_out, not_6_out, not_7_out, not_8_out, not_9_out, not_10_out,
       not_11_out, not_12_out, not_13_out, not_14_out, not_15_out, not_16_out, not_17_out, not_18_out,
       not_19_out, not_20_out, not_21_out;

  not not_1 (not_1_out, i[2]);
  not not_2 (not_2_out, i[0]);
  not not_3 (not_3_out, i[2]);
  not not_4 (not_4_out, i[1]);
  not not_5 (not_5_out, i[0]);
  not not_6 (not_6_out, i[1]);
  not not_7 (not_7_out, i[2]);
  not not_8 (not_8_out, i[0]);
  not not_9 (not_9_out, i[2]);
  not not_10 (not_10_out, i[0]);
  not not_11 (not_11_out, i[1]);
  not not_12 (not_12_out, i[2]);
  not not_13 (not_13_out, i[0]);
  not not_14 (not_14_out, i[0]);
  not not_15 (not_15_out, i[1]);
  not not_16 (not_16_out, i[0]);
  not not_17 (not_17_out, i[1]);
  not not_18 (not_18_out, i[0]);
  not not_19 (not_19_out, i[0]);
  not not_20 (not_20_out, i[1]);
  not not_21 (not_21_out, i[2]);
  and and_1 (and_1_out, not_1_out, not_2_out);
  and and_2 (and_2_out, i[2], i[0]);
  and and_3 (and_3_out, i[1], i[0]);
  and and_4 (and_4_out, not_4_out, not_5_out);
  and and_5 (and_5_out, not_7_out, not_8_out);
  and and_6 (and_6_out, not_9_out, i[1]);
  and and_7 (and_7_out, i[1], not_10_out);
  and and_8 (and_8_out, not_12_out, not_13_out);
  and and_9 (and_9_out, i[1], not_14_out);
  and and_10 (and_10_out, not_15_out, not_16_out);
  and and_11 (and_11_out, i[2], not_17_out);
  and and_12 (and_12_out, i[2], not_18_out);
  and and_13 (and_13_out, i[1], not_19_out);
  and and_14 (and_14_out, i[2], not_20_out);
  and and_15 (and_15_out, not_21_out, i[1]);
  or or_1 (c, not_6_out, i[2], i[0]);
  and and_16 (and_16_out, i[2], not_11_out, i[0]);
  or or_2 (a, i[3], i[1], and_1_out, and_2_out);
  or or_3 (b, not_3_out, and_3_out, and_4_out);
  or or_4 (d, i[3], and_5_out, and_6_out, and_7_out, and_16_out);
  or or_5 (e, and_8_out, and_9_out);
  or or_6 (f, i[3], and_10_out, and_11_out, and_12_out);
  or or_7 (g, i[3], and_13_out, and_14_out, and_15_out);

  // Other names for the same wires on the sheet: a1 = a; b1 = b; c1 = c; d1 = d; e1 = e; f1 = f; g1 = g; D_t = i[0];
  //   C_t = i[1]; B_t = i[2]; A_t = i[3]
endmodule
