// Logisim project 6.circ as structural Verilog: 1 circuit, main circuit multiplexor
module multiplexor (
  input  [2:0] inputzero,
  input  [2:0] inputone,
  input  [2:0] inputtwo,
  input  [2:0] inputthree,
  input  [1:0] selector,
  output [2:0] muxoutput
);

  wire and_1_out, and_2_out, and_3_out, and_4_out, and_5_out, and_6_out, and_7_out, and_8_out, and_9_out,
       and_10_out, and_11_out, and_12_out, not_1_out, not_2_out, not_3_out, not_4_out, not_5_out, not_6_out;

  not not_1 (not_1_out, selector[1]);
  not not_2 (not_2_out, selector[1]);
  not not_3 (not_3_out, selector[1]);
  not not_4 (not_4_out, selector[0]);
  not not_5 (not_5_out, selector[0]);
  not not_6 (not_6_out, selector[0]);
  and and_1 (and_1_out, not_4_out, inputzero[0], not_1_out);
  and and_2 (and_2_out, selector[0], inputone[0], not_1_out);
  and and_3 (and_3_out, not_4_out, inputtwo[0], selector[1]);
  and and_4 (and_4_out, selector[0], inputthree[0], selector[1]);
  and and_5 (and_5_out, not_5_out, inputzero[2], not_2_out);
  and and_6 (and_6_out, selector[0], inputone[2], not_2_out);
  and and_7 (and_7_out, not_5_out, inputtwo[2], selector[1]);
  and and_8 (and_8_out, selector[0], inputthree[2], selector[1]);
  and and_9 (and_9_out, not_6_out, inputzero[1], not_3_out);
  and and_10 (and_10_out, selector[0], inputone[1], not_3_out);
  and and_11 (and_11_out, not_6_out, inputtwo[1], selector[1]);
  and and_12 (and_12_out, selector[0], inputthree[1], selector[1]);
  or or_1 (muxoutput[0], and_1_out, and_2_out, and_3_out, and_4_out);
  or or_2 (muxoutput[2], and_5_out, and_6_out, and_7_out, and_8_out);
  or or_3 (muxoutput[1], and_9_out, and_10_out, and_11_out, and_12_out);

  // Other names for the same wires on the sheet: input0[2:0] = inputzero; input00 = inputzero[0];
  //   input01 = inputzero[1]; input02 = inputzero[2]; input1[2:0] = inputone; input10 = inputone[0];
  //   input11 = inputone[1]; input12 = inputone[2]; input2[2:0] = inputtwo; input20 = inputtwo[0];
  //   input21 = inputtwo[1]; input22 = inputtwo[2]; input3[2:0] = inputthree; input30 = inputthree[0];
  //   input31 = inputthree[1]; input32 = inputthree[2]; O[2:0] = muxoutput; S0 = muxoutput[0]; S1 = muxoutput[1];
  //   S2 = muxoutput[2]; S[1:0] = selector; s1_t = selector[0]; s2_t = selector[1]
endmodule
