// Logisim project extracredit.circ as structural Verilog: 1 circuit, main circuit tripledigit
module tripledigit (
  input  [9:0] thousand,
  output [6:0] hundreds,
  output [6:0] tens,
  output [6:0] ones
);

  wire A, A1, A2, and_1_out, and_2_out, and_3_out, and_4_out, and_5_out, and_6_out, and_7_out, and_8_out,
       and_9_out, and_10_out, and_11_out, and_12_out, and_13_out, and_14_out, and_15_out, and_16_out,
       and_17_out, and_18_out, and_19_out, and_20_out, and_21_out, and_22_out, and_23_out, and_24_out,
       and_25_out, and_26_out, and_27_out, and_28_out, and_29_out, and_30_out, and_31_out, and_32_out,
       and_33_out, and_34_out, and_35_out, and_36_out, and_37_out, and_38_out, and_39_out, and_40_out,
       and_41_out, and_42_out, and_43_out, and_44_out, and_45_out, and_46_out, and_47_out, and_48_out, B, B1,
       B2, C, C1, C2, D, D1, D2, not_1_out, not_2_out, not_3_out, not_4_out, not_5_out, not_6_out, not_7_out,
       not_8_out, not_9_out, not_10_out, not_11_out, not_12_out, not_13_out, not_14_out, not_15_out,
       not_16_out, not_17_out, not_18_out, not_19_out, not_20_out, not_21_out, not_22_out, not_23_out,
       not_24_out, not_25_out, not_26_out, not_27_out, not_28_out, not_29_out, not_30_out, not_31_out,
       not_32_out, not_33_out, not_34_out, not_35_out, not_36_out, not_37_out, not_38_out, not_39_out,
       not_40_out, not_41_out, not_42_out, not_43_out, not_44_out, not_45_out, not_46_out, not_47_out,
       not_48_out, not_49_out, not_50_out, not_51_out, not_52_out, not_53_out, not_54_out, not_55_out,
       not_56_out, not_57_out, not_58_out, not_59_out, not_60_out, not_61_out, not_62_out, not_63_out;
  wire [9:0] rem1;
  wire [9:4] Hundreds1, rem2, Tens1;

  not not_1 (not_1_out, B);
  not not_2 (not_2_out, D);
  not not_3 (not_3_out, B);
  not not_4 (not_4_out, C);
  not not_5 (not_5_out, D);
  not not_6 (not_6_out, C);
  not not_7 (not_7_out, B);
  not not_8 (not_8_out, D);
  not not_9 (not_9_out, B);
  not not_10 (not_10_out, D);
  not not_11 (not_11_out, C);
  not not_12 (not_12_out, B);
  not not_13 (not_13_out, D);
  not not_14 (not_14_out, D);
  not not_15 (not_15_out, C);
  not not_16 (not_16_out, D);
  not not_17 (not_17_out, C);
  not not_18 (not_18_out, D);
  not not_19 (not_19_out, D);
  not not_20 (not_20_out, C);
  not not_21 (not_21_out, B);
  not not_22 (not_22_out, B1);
  not not_23 (not_23_out, D1);
  not not_24 (not_24_out, B1);
  not not_25 (not_25_out, C1);
  not not_26 (not_26_out, D1);
  not not_27 (not_27_out, C1);
  not not_28 (not_28_out, B1);
  not not_29 (not_29_out, D1);
  not not_30 (not_30_out, B1);
  not not_31 (not_31_out, D1);
  not not_32 (not_32_out, C1);
  not not_33 (not_33_out, B1);
  not not_34 (not_34_out, D1);
  not not_35 (not_35_out, D1);
  not not_36 (not_36_out, C1);
  not not_37 (not_37_out, D1);
  not not_38 (not_38_out, C1);
  not not_39 (not_39_out, D1);
  not not_40 (not_40_out, D1);
  not not_41 (not_41_out, C1);
  not not_42 (not_42_out, B1);
  not not_43 (not_43_out, B2);
  not not_44 (not_44_out, D2);
  not not_45 (not_45_out, B2);
  not not_46 (not_46_out, C2);
  not not_47 (not_47_out, D2);
  not not_48 (not_48_out, C2);
  not not_49 (not_49_out, B2);
  not not_50 (not_50_out, D2);
  not not_51 (not_51_out, B2);
  not not_52 (not_52_out, D2);
  not not_53 (not_53_out, C2);
  not not_54 (not_54_out, B2);
  not not_55 (not_55_out, D2);
  not not_56 (not_56_out, D2);
  not not_57 (not_57_out, C2);
  not not_58 (not_58_out, D2);
  not not_59 (not_59_out, C2);
  not not_60 (not_60_out, D2);
  not not_61 (not_61_out, D2);
  not not_62 (not_62_out, C2);
  not not_63 (not_63_out, B2);
  and and_1 (and_1_out, not_1_out, not_2_out);
  and and_2 (and_2_out, B, D);
  and and_3 (and_3_out, C, D);
  and and_4 (and_4_out, not_4_out, not_5_out);
  and and_5 (and_5_out, not_7_out, not_8_out);
  and and_6 (and_6_out, not_9_out, C);
  and and_7 (and_7_out, C, not_10_out);
  and and_8 (and_8_out, B, not_11_out, D);
  and and_9 (and_9_out, not_12_out, not_13_out);
  and and_10 (and_10_out, C, not_14_out);
  and and_11 (and_11_out, not_15_out, not_16_out);
  and and_12 (and_12_out, B, not_17_out);
  and and_13 (and_13_out, B, not_18_out);
  and and_14 (and_14_out, C, not_19_out);
  and and_15 (and_15_out, B, not_20_out);
  and and_16 (and_16_out, not_21_out, C);
  Divider #(.width(10)) divider_1 (
    .a(rem1), .b(10'ha), .out({Tens1, A1, B1, C1, D1}), .rem({rem2, A2, B2, C2, D2}));  // open: upper
  and and_17 (and_17_out, not_22_out, not_23_out);
  and and_18 (and_18_out, B1, D1);
  and and_19 (and_19_out, C1, D1);
  and and_20 (and_20_out, not_25_out, not_26_out);
  and and_21 (and_21_out, not_28_out, not_29_out);
  and and_22 (and_22_out, not_30_out, C1);
  and and_23 (and_23_out, C1, not_31_out);
  and and_24 (and_24_out, not_33_out, not_34_out);
  and and_25 (and_25_out, C1, not_35_out);
  and and_26 (and_26_out, not_36_out, not_37_out);
  and and_27 (and_27_out, B1, not_38_out);
  and and_28 (and_28_out, B1, not_39_out);
  and and_29 (and_29_out, C1, not_40_out);
  and and_30 (and_30_out, B1, not_41_out);
  and and_31 (and_31_out, not_42_out, C1);
  and and_32 (and_32_out, not_43_out, not_44_out);
  and and_33 (and_33_out, B2, D2);
  and and_34 (and_34_out, C2, D2);
  and and_35 (and_35_out, not_46_out, not_47_out);
  and and_36 (and_36_out, not_49_out, not_50_out);
  and and_37 (and_37_out, not_51_out, C2);
  and and_38 (and_38_out, C2, not_52_out);
  and and_39 (and_39_out, not_54_out, not_55_out);
  and and_40 (and_40_out, C2, not_56_out);
  and and_41 (and_41_out, not_57_out, not_58_out);
  and and_42 (and_42_out, B2, not_59_out);
  and and_43 (and_43_out, B2, not_60_out);
  and and_44 (and_44_out, C2, not_61_out);
  and and_45 (and_45_out, B2, not_62_out);
  and and_46 (and_46_out, not_63_out, C2);
  Divider #(.width(10)) divider_2 (.a(thousand), .b(10'h64), .out({Hundreds1, A, B, C, D}), .rem(rem1));  // open: upper
  or or_1 (hundreds[5], not_3_out, and_3_out, and_4_out);
  or or_2 (hundreds[4], not_6_out, B, D);
  or or_3 (hundreds[2], and_9_out, and_10_out);
  or or_4 (tens[4], not_27_out, B1, D1);
  and and_47 (and_47_out, B1, not_32_out, D1);
  or or_5 (ones[4], not_48_out, B2, D2);
  and and_48 (and_48_out, B2, not_53_out, D2);
  or or_6 (hundreds[6], A, C, and_1_out, and_2_out);
  or or_7 (hundreds[3], A, and_5_out, and_6_out, and_7_out, and_8_out);
  or or_8 (hundreds[1], A, and_11_out, and_12_out, and_13_out);
  or or_9 (hundreds[0], A, and_14_out, and_15_out, and_16_out);
  or or_10 (tens[6], A1, C1, and_17_out, and_18_out);
  or or_11 (tens[5], not_24_out, and_19_out, and_20_out);
  or or_12 (tens[3], A1, and_21_out, and_22_out, and_23_out, and_47_out);
  or or_13 (tens[2], and_24_out, and_25_out);
  or or_14 (tens[1], A1, and_26_out, and_27_out, and_28_out);
  or or_15 (tens[0], A1, and_29_out, and_30_out, and_31_out);
  or or_16 (ones[6], A2, C2, and_32_out, and_33_out);
  or or_17 (ones[5], not_45_out, and_34_out, and_35_out);
  or or_18 (ones[3], A2, and_36_out, and_37_out, and_38_out, and_48_out);
  or or_19 (ones[2], and_39_out, and_40_out);
  or or_20 (ones[1], A2, and_41_out, and_42_out, and_43_out);
  or or_21 (ones[0], A2, and_44_out, and_45_out, and_46_out);

  // Other names for the same wires on the sheet: g1 = hundreds[0]; f1 = hundreds[1]; e1 = hundreds[2];
  //   d1_t = hundreds[3]; c1_t = hundreds[4]; b1_t = hundreds[5]; a1_t = hundreds[6]; Hundreds1[3:0] = {A, B, C, D};
  //   Hundreds2[3:0] = {A, B, C, D}; g3 = ones[0]; f3 = ones[1]; e3 = ones[2]; d3 = ones[3]; c3 = ones[4];
  //   b3 = ones[5]; a3 = ones[6]; Ones2[3:0] = {A2, B2, C2, D2}; rem2[3:0] = {A2, B2, C2, D2}; g2 = tens[0];
  //   f2 = tens[1]; e2 = tens[2]; d2_t = tens[3]; c2_t = tens[4]; b2_t = tens[5]; a2_t = tens[6];
  //   Tens1[3:0] = {A1, B1, C1, D1}; Tens2[3:0] = {A1, B1, C1, D1}
endmodule
