// Logisim project 1.circ as structural Verilog: 1 circuit, main circuit muxfunction
module muxfunction (
  input  [3:0] fourbitinput,
  output f
);

  Multiplexer #(.select(4), .enable("false")) multiplexer_1 (
    .in0(1'b1), .in1(1'b1), .in2(1'b0), .in3(1'b1), .in4(1'b0), .in5(1'b1), .in6(1'b0), .in7(1'b0),
    .in8(1'b0), .in9(1'b1), .in10(1'b0), .in11(1'b1), .in12(1'b1), .in13(1'b0), .in14(1'b0), .in15(1'b0),
    .out(f), .sel(fourbitinput));

  // Other names for the same wires on the sheet: a[3:0] = fourbitinput
endmodule
