// Logisim project 3.circ as structural Verilog: 1 circuit, main circuit bitcounting
module bitcounting (
  input  [11:0] twelvebitinput,
  output [3:0] zeroes
);

  wire [3:0] bitadder_1_out;

  BitAdder #(.width(12)) bitadder_1 (.in0(twelvebitinput), .out(bitadder_1_out));
  Subtractor #(.width(4)) subtractor_1 (.a(4'b1100), .b(bitadder_1_out), .out(zeroes));  // open: bin, bout

  // Other names for the same wires on the sheet: a[11:0] = twelvebitinput
endmodule
