// Logisim project 4.circ as structural Verilog: 1 circuit, main circuit comparison
module comparison (
  input  [7:0] inputa,
  input  [7:0] inputb,
  output areequal
);

  wire not_1_out, not_2_out, not_3_out, not_4_out, not_5_out, not_6_out, not_7_out, not_8_out, xor_1_out,
       xor_2_out, xor_3_out, xor_4_out, xor_5_out, xor_6_out, xor_7_out, xor_8_out;

  xor xor_1 (xor_1_out, inputa[0], inputb[0]);
  xor xor_2 (xor_2_out, inputa[4], inputb[4]);
  not not_1 (not_1_out, xor_1_out);
  xor xor_3 (xor_3_out, inputa[2], inputb[2]);
  xor xor_4 (xor_4_out, inputa[1], inputb[1]);
  xor xor_5 (xor_5_out, inputa[5], inputb[5]);
  xor xor_6 (xor_6_out, inputa[6], inputb[6]);
  xor xor_7 (xor_7_out, inputa[3], inputb[3]);
  xor xor_8 (xor_8_out, inputa[7], inputb[7]);
  not not_2 (not_2_out, xor_5_out);
  not not_3 (not_3_out, xor_4_out);
  not not_4 (not_4_out, xor_3_out);
  not not_5 (not_5_out, xor_2_out);
  not not_6 (not_6_out, xor_7_out);
  not not_7 (not_7_out, xor_8_out);
  not not_8 (not_8_out, xor_6_out);
  and and_1 (areequal, not_1_out, not_3_out, not_4_out, not_6_out, not_7_out, not_8_out, not_2_out, not_5_out);

  // Other names for the same wires on the sheet: a[7:0] = inputa; b[7:0] = inputb
endmodule
