// Logisim project 5.circ as structural Verilog: 1 circuit, main circuit parity
module parity (
  input  [9:0] tenbitinput,
  output [10:0] evenparity
);

  wire [3:0] bitadder_1_out, divider_1_rem;

  BitAdder #(.width(10)) bitadder_1 (.in0(tenbitinput), .out(bitadder_1_out));
  Divider #(.width(4)) divider_1 (.a(bitadder_1_out), .b(4'b0010), .rem(divider_1_rem));  // open: out, upper
  Comparator #(.width(4)) comparator_1 (.a(divider_1_rem), .b(4'b0001), .eq(evenparity[0]));  // open: gt, lt

  assign evenparity[10:1] = tenbitinput;

  // Other names for the same wires on the sheet: a[9:0] = tenbitinput; b[10:0] = {tenbitinput, evenparity[0]};
  //   c = evenparity[0]
endmodule
