// Logisim project 6.circ as structural Verilog: 1 circuit, main circuit cla
module cla (
  input  [3:0] inputa,
  input  [3:0] inputb,
  input  carryin,
  output [3:0] carryout,
  output [3:0] generator,
  output [3:0] propagator
);

  wire and_5_out, and_6_out, and_7_out, and_8_out, and_9_out, and_10_out, and_11_out, and_12_out, and_13_out,
       and_14_out;

  xor xor_1 (propagator[0], inputa[0], inputb[0]);
  and and_1 (generator[0], inputa[0], inputb[0]);
  xor xor_2 (propagator[1], inputa[1], inputb[1]);
  and and_2 (generator[1], inputa[1], inputb[1]);
  xor xor_3 (propagator[2], inputa[2], inputb[2]);
  and and_3 (generator[2], inputa[2], inputb[2]);
  xor xor_4 (propagator[3], inputa[3], inputb[3]);
  and and_4 (generator[3], inputa[3], inputb[3]);
  and and_5 (and_5_out, propagator[0], carryin);
  and and_6 (and_6_out, propagator[1], generator[0]);
  and and_7 (and_7_out, propagator[1], propagator[0], carryin);
  and and_8 (and_8_out, propagator[2], generator[1]);
  and and_9 (and_9_out, propagator[2], propagator[1], generator[0]);
  and and_10 (and_10_out, propagator[2], propagator[1], propagator[0], carryin);
  and and_11 (and_11_out, propagator[3], generator[2]);
  and and_12 (and_12_out, propagator[3], propagator[2], generator[1]);
  and and_13 (and_13_out, propagator[3], propagator[2], propagator[1], generator[0]);
  and and_14 (and_14_out, propagator[3], propagator[2], propagator[1], propagator[0], carryin);
  or or_1 (carryout[0], generator[0], and_5_out);
  or or_2 (carryout[1], generator[1], and_6_out, and_7_out);
  or or_3 (carryout[2], generator[2], and_8_out, and_9_out, and_10_out);
  or or_4 (carryout[3], generator[3], and_11_out, and_12_out, and_13_out, and_14_out);
endmodule
