// Logisim project 7.circ as structural Verilog: 2 circuits, main circuit alu
module alu (
  input  [3:0] inputa,
  input  [3:0] inputb,
  input  [2:0] operation,
  output [3:0] aluout
);

  wire c1, c2, c3, xor_2_out, xor_3_out, xor_5_out, xor_8_out;
  wire [3:0] ad, and_1_out, complementb, not_1_out, not_2_out, not_3_out, or_1_out, sub, xor_1_out;
  wire [3:3] carryout;

  assign not_1_out = ~inputb;  // NOT_Gate not_1, 4 bits wide
  assign and_1_out = inputa & inputb;  // AND_Gate and_1, 4 bits wide
  assign not_2_out = ~inputb;  // NOT_Gate not_2, 4 bits wide
  assign or_1_out = inputa | inputb;  // OR_Gate or_1, 4 bits wide
  assign xor_1_out = inputa ^ inputb;  // XOR_Gate xor_1, 4 bits wide
  assign not_3_out = ~inputa;  // NOT_Gate not_3, 4 bits wide
  cla cla_1 (
    .inputa(inputa), .inputb(inputb), .carryin(1'b0), .carryout({carryout[3], c3, c2, c1}));  // open: generator, propagator
  add add_1 (.in_1(not_1_out), .in_2(4'b0001), .out_3(complementb));
  add add_2 (.in_1(complementb), .in_2(inputa), .out_3(sub));
  xor xor_2 (xor_2_out, inputa[1], inputb[1]);
  xor xor_3 (xor_3_out, inputa[0], inputb[0]);
  xor xor_4 (ad[1], xor_2_out, c1);
  xor xor_5 (xor_5_out, inputa[2], inputb[2]);
  xor xor_6 (ad[0], xor_3_out, 1'b0);
  xor xor_7 (ad[2], xor_5_out, c2);
  Multiplexer #(.select(3), .width(4), .enable("false")) multiplexer_1 (
    .in0(and_1_out), .in1(not_2_out), .in2(or_1_out), .in3(sub), .in4(xor_1_out), .in5(not_3_out), .in6(ad),
    .out(aluout), .sel(operation));  // open: in7
  xor xor_8 (xor_8_out, inputa[3], inputb[3]);
  xor xor_9 (ad[3], xor_8_out, c3);

  // Other names for the same wires on the sheet: s1 = ad[0]; s2 = ad[1]; s3 = ad[2]; s4 = ad[3];
  //   carryout[2:0] = {c3, c2, c1}; a1 = inputa[0]; a2 = inputa[1]; a3 = inputa[2]; a4 = inputa[3]; b1 = inputb[0];
  //   b2 = inputb[1]; b3 = inputb[2]; b4 = inputb[3]
endmodule

module add (
  input  [3:0] in_1,
  input  [3:0] in_2,
  output [3:0] out_3
);

  wire c1, c2, c3, xor_1_out, xor_2_out, xor_4_out, xor_7_out;
  wire [3:3] carryout;

  cla cla_1 (
    .inputa(in_1), .inputb(in_2), .carryin(1'b0), .carryout({carryout[3], c3, c2, c1}));  // open: generator, propagator
  xor xor_1 (xor_1_out, in_1[1], in_2[1]);
  xor xor_2 (xor_2_out, in_1[0], in_2[0]);
  xor xor_3 (out_3[1], xor_1_out, c1);
  xor xor_4 (xor_4_out, in_1[2], in_2[2]);
  xor xor_5 (out_3[0], xor_2_out, 1'b0);
  xor xor_6 (out_3[2], xor_4_out, c2);
  xor xor_7 (xor_7_out, in_1[3], in_2[3]);
  xor xor_8 (out_3[3], xor_7_out, c3);

  // Other names for the same wires on the sheet: carryout[2:0] = {c3, c2, c1}; a1 = in_1[0]; inputa[3:0] = in_1;
  //   a2 = in_1[1]; a3 = in_1[2]; a4 = in_1[3]; b1 = in_2[0]; inputb[3:0] = in_2; b2 = in_2[1]; b3 = in_2[2];
  //   b4 = in_2[3]; s1 = out_3[0]; s2 = out_3[1]; s3 = out_3[2]; s4 = out_3[3]
endmodule
