// Logisim project 8.circ as structural Verilog: 2 circuits, main circuit errorcorrecting
module errorcorrecting (
  input  [14:0] inputdata,
  output [10:0] correcteddata
);

  wire [3:0] c, position;
  wire [10:0] ff;

  Decoder #(.select(4)) decoder_1 (
    .out3(ff[0]), .out5(ff[1]), .out6(ff[2]), .out7(ff[3]), .out9(ff[4]), .out10(ff[5]), .out11(ff[6]),
    .out12(ff[7]), .out13(ff[8]), .out14(ff[9]), .out15(ff[10]), .sel(position));  // open: out0, out1, out2, out4, out8, en
  assign position = c ^ {inputdata[7], inputdata[3], inputdata[1:0]};  // XOR_Gate xor_1, 4 bits wide
  parity parity_1 (.in_1({inputdata[14:11], inputdata[6:4]}), .out_2(c[2]));
  assign correcteddata = ff ^ {inputdata[14:8], inputdata[6:4], inputdata[2]};  // XOR_Gate xor_2, 11 bits wide
  parity parity_2 (
    .in_1({inputdata[14], inputdata[12], inputdata[10], inputdata[8], inputdata[6], inputdata[4], inputdata[2]}),
    .out_2(c[0]));
  parity parity_3 (.in_1(inputdata[14:8]), .out_2(c[3]));
  parity parity_4 (.in_1({inputdata[14:13], inputdata[10:9], inputdata[6:5], inputdata[2]}), .out_2(c[1]));

  // Other names for the same wires on the sheet: c1 = c[0]; c2 = c[1]; c3 = c[2]; c4 = c[3]; a[14:0] = inputdata;
  //   c0i = inputdata[0]; ci[3:0] = {inputdata[7], inputdata[3], inputdata[1:0]}; c1i = inputdata[1];
  //   c2i = inputdata[3]; c3i = inputdata[7]; d[10:0] = {inputdata[14:8], inputdata[6:4], inputdata[2]};
  //   d0 = inputdata[2]; d1 = inputdata[4]; d2 = inputdata[5]; d3 = inputdata[6]; d4 = inputdata[8];
  //   d5 = inputdata[9]; d6 = inputdata[10]; d7 = inputdata[11]; d8 = inputdata[12]; d9 = inputdata[13];
  //   d10 = inputdata[14]; opt[10:0] = correcteddata
endmodule

module parity (
  input  [6:0] in_1,
  output out_2
);

  wire [2:0] bitadder_1_out, divider_1_rem;

  BitAdder #(.width(7)) bitadder_1 (.in0(in_1), .out(bitadder_1_out));
  Divider #(.width(3)) divider_1 (.a(bitadder_1_out), .b(3'b010), .rem(divider_1_rem));  // open: out, upper
  Comparator #(.width(3)) comparator_1 (.a(divider_1_rem), .b(3'b001), .eq(out_2));  // open: gt, lt

  // Other names for the same wires on the sheet: a[6:0] = in_1
endmodule
