// Logisim project 2.circ as structural Verilog: 1 circuit, main circuit tregister
module tregister (
  input  [7:0] eightbitinput,
  input  sysclock,
  output [7:0] registerval
);

  wire xor_1_out, xor_2_out, xor_3_out, xor_4_out, xor_5_out, xor_6_out, xor_7_out, xor_8_out;

  xor xor_1 (xor_1_out, eightbitinput[0], registerval[0]);
  T_Flip_Flop t_ff_1 (.T(xor_1_out), .clk(sysclock), .Q(registerval[0]));  // open: Qn, reset, preset
  xor xor_2 (xor_2_out, eightbitinput[2], registerval[2]);
  T_Flip_Flop t_ff_2 (.T(xor_2_out), .clk(sysclock), .Q(registerval[2]));  // open: Qn, reset, preset
  xor xor_3 (xor_3_out, eightbitinput[4], registerval[4]);
  T_Flip_Flop t_ff_3 (.T(xor_3_out), .clk(sysclock), .Q(registerval[4]));  // open: Qn, reset, preset
  xor xor_4 (xor_4_out, eightbitinput[6], registerval[6]);
  T_Flip_Flop t_ff_4 (.T(xor_4_out), .clk(sysclock), .Q(registerval[6]));  // open: Qn, reset, preset
  T_Flip_Flop t_ff_5 (.T(xor_6_out), .clk(sysclock), .Q(registerval[1]));  // open: Qn, reset, preset
  T_Flip_Flop t_ff_6 (.T(xor_7_out), .clk(sysclock), .Q(registerval[3]));  // open: Qn, reset, preset
  xor xor_5 (xor_5_out, eightbitinput[5], registerval[5]);
  T_Flip_Flop t_ff_7 (.T(xor_5_out), .clk(sysclock), .Q(registerval[5]));  // open: Qn, reset, preset
  T_Flip_Flop t_ff_8 (.T(xor_8_out), .clk(sysclock), .Q(registerval[7]));  // open: Qn, reset, preset
  xor xor_6 (xor_6_out, eightbitinput[1], registerval[1]);
  xor xor_7 (xor_7_out, eightbitinput[3], registerval[3]);
  xor xor_8 (xor_8_out, eightbitinput[7], registerval[7]);

  // Other names for the same wires on the sheet: bit[7:0] = eightbitinput; one = eightbitinput[0];
  //   two = eightbitinput[1]; three = eightbitinput[2]; four = eightbitinput[3]; five = eightbitinput[4];
  //   six = eightbitinput[5]; seven = eightbitinput[6]; eight = eightbitinput[7]; clo = sysclock;
  //   final[7:0] = registerval; oone = registerval[0]; otwo = registerval[1]; othree = registerval[2];
  //   ofour = registerval[3]; ofive = registerval[4]; osix = registerval[5]; oseven = registerval[6];
  //   oeight = registerval[7]
endmodule
