// Logisim project 3.circ as structural Verilog: 1 circuit, main circuit fsmtable
module fsmtable (
  input  inputu,
  input  sysclock,
  output outputn
);

  wire and_1_out, and_2_out, and_3_out, and_4_out, and_5_out, ap, b, bp, na, nb, not_1_out, not_2_out;

  D_Flip_Flop a (.D(ap), .clk(sysclock), .Q(outputn), .Qn(na));  // open: preset, reset
  D_Flip_Flop u_b (.D(bp), .clk(sysclock), .Q(b), .Qn(nb));  // open: preset, reset
  not not_1 (not_1_out, inputu);
  not not_2 (not_2_out, inputu);
  and and_1 (and_1_out, not_1_out, na);
  and and_2 (and_2_out, b, inputu);
  and and_3 (and_3_out, na, not_2_out);
  and and_4 (and_4_out, na, b);
  and and_5 (and_5_out, outputn, inputu, nb);
  or or_1 (ap, and_1_out, and_2_out);
  or or_2 (bp, and_3_out, and_4_out, and_5_out);

  // Other names for the same wires on the sheet: clo = sysclock; a = outputn; f = outputn; i = inputu
endmodule
