// Logisim project 4.circ as structural Verilog: 1 circuit, main circuit fsmdiagram
module fsmdiagram (
  input  inputv,
  input  sysclock,
  output outputp
);

  wire a, and_1_out, and_2_out, and_3_out, and_4_out, and_5_out, and_6_out, and_7_out, and_8_out, and_9_out,
       and_10_out, and_11_out, and_12_out, and_13_out, and_14_out, and_15_out, ap, b, bp, c, cp, na, nb, nc,
       not_1_out, not_2_out, not_3_out;

  D_Flip_Flop d_ff_1 (.D(ap), .clk(sysclock), .Q(a), .Qn(na));  // open: preset, reset
  D_Flip_Flop d_ff_2 (.D(bp), .clk(sysclock), .Q(b), .Qn(nb));  // open: preset, reset
  D_Flip_Flop d_ff_3 (.D(cp), .clk(sysclock), .Q(c), .Qn(nc));  // open: preset, reset
  not not_1 (not_1_out, inputv);
  and and_1 (and_1_out, b, nc);
  and and_2 (and_2_out, a, b);
  and and_3 (and_3_out, a, nc);
  and and_4 (and_4_out, nc, nb, inputv);
  and and_5 (and_5_out, na, b, not_1_out);
  and and_6 (and_6_out, a, nb);
  or or_1 (outputp, and_1_out, and_2_out, and_3_out);
  or or_2 (bp, and_4_out, and_5_out, and_6_out);
  and and_7 (and_7_out, b, nc, inputv);
  and and_8 (and_8_out, a, nc);
  and and_9 (and_9_out, nb, c);
  and and_10 (and_10_out, na, c);
  not not_2 (not_2_out, inputv);
  not not_3 (not_3_out, inputv);
  or or_3 (ap, and_7_out, and_8_out, and_9_out, and_10_out);
  and and_11 (and_11_out, na, nb, not_2_out);
  and and_12 (and_12_out, nc, not_3_out);
  and and_13 (and_13_out, a, nc);
  and and_14 (and_14_out, a, nb, inputv);
  and and_15 (and_15_out, na, b, c, inputv);
  or or_4 (cp, and_11_out, and_12_out, and_13_out, and_14_out, and_15_out);

  // Other names for the same wires on the sheet: clo = sysclock; f = outputp; i = inputv
endmodule
