// Logisim project 5.circ as structural Verilog: 1 circuit, main circuit paritygen
module paritygen (
  input  inputw,
  input  sysclock,
  output outputq
);

  wire a, and_1_out, and_2_out, and_3_out, and_4_out, and_5_out, and_6_out, and_7_out, and_8_out, and_9_out,
       and_10_out, ap, b, bp, c, cp, na, nb, nc, not_1_out, not_2_out, not_3_out, not_4_out, not_5_out;

  not not_1 (not_1_out, inputw);
  D_Flip_Flop d_ff_1 (.D(ap), .clk(sysclock), .Q(a), .Qn(na));  // open: preset, reset
  D_Flip_Flop d_ff_2 (.D(bp), .clk(sysclock), .Q(b), .Qn(nb));  // open: preset, reset
  D_Flip_Flop d_ff_3 (.D(cp), .clk(sysclock), .Q(c), .Qn(nc));  // open: preset, reset
  not not_2 (not_2_out, inputw);
  and and_1 (and_1_out, nb, not_2_out);
  and and_2 (and_2_out, na, b, inputw);
  and and_3 (and_3_out, a, not_1_out);
  not not_3 (not_3_out, inputw);
  or or_1 (cp, and_1_out, and_2_out, and_3_out);
  and and_4 (and_4_out, nb, c, not_3_out);
  and and_5 (and_5_out, b, nc, not_4_out);
  not not_4 (not_4_out, inputw);
  and and_6 (and_6_out, na, inputw);
  and and_7 (and_7_out, c, inputw);
  not not_5 (not_5_out, inputw);
  and and_8 (and_8_out, nc, b, not_5_out);
  and and_9 (and_9_out, na, c, inputw);
  or or_2 (bp, and_4_out, and_5_out, and_6_out, and_7_out);
  and and_10 (and_10_out, b, nc);
  or or_3 (ap, and_8_out, and_9_out);
  or or_4 (outputq, and_10_out, a);

  // Other names for the same wires on the sheet: clo = sysclock; f = outputq; i = inputw
endmodule
