// Logisim project 6.circ as structural Verilog: 1 circuit, main circuit sequencecheck
module sequencecheck (
  input  inputx,
  input  sysclock,
  output outputr
);

  wire a, and_1_out, and_2_out, and_3_out, and_4_out, and_6_out, and_7_out, and_8_out, and_9_out, and_10_out,
       and_11_out, and_12_out, and_13_out, and_14_out, ap, b, bp, c, cp, na, nb, nc, not_1_out, not_2_out,
       not_3_out, not_4_out, not_5_out;

  D_Flip_Flop d_ff_1 (.D(ap), .clk(sysclock), .Q(a), .Qn(na));  // open: preset, reset
  D_Flip_Flop d_ff_2 (.D(bp), .clk(sysclock), .Q(b), .Qn(nb));  // open: preset, reset
  D_Flip_Flop d_ff_3 (.D(cp), .clk(sysclock), .Q(c), .Qn(nc));  // open: preset, reset
  not not_1 (not_1_out, inputx);
  not not_2 (not_2_out, inputx);
  and and_1 (and_1_out, b, nc, not_1_out);
  and and_2 (and_2_out, na, b);
  and and_3 (and_3_out, na, not_2_out);
  and and_4 (and_4_out, a, nb, c, inputx);
  not not_3 (not_3_out, inputx);
  and and_5 (outputr, a, nc, nb, not_3_out);
  or or_1 (bp, and_1_out, and_2_out, and_3_out, and_4_out);
  not not_4 (not_4_out, inputx);
  and and_6 (and_6_out, nb, c, inputx);
  and and_7 (and_7_out, a, nb, c);
  and and_8 (and_8_out, b, nc, not_4_out);
  and and_9 (and_9_out, a, b, nc);
  and and_10 (and_10_out, na, b, c);
  not not_5 (not_5_out, inputx);
  and and_11 (and_11_out, nb, c, inputx);
  and and_12 (and_12_out, na, inputx);
  and and_13 (and_13_out, a, b, nc, not_5_out);
  and and_14 (and_14_out, na, c);
  or or_2 (cp, and_13_out, and_11_out, and_12_out, and_14_out);
  or or_3 (ap, and_6_out, and_7_out, and_8_out, and_9_out, and_10_out);

  // Other names for the same wires on the sheet: clo = sysclock; f = outputr; i = inputx
endmodule
