// Logisim project 7.circ as structural Verilog: 1 circuit, main circuit vendingmachine
module vendingmachine (
  input  input5,
  input  input10,
  input  input20,
  input  sysclock,
  output outputcoke,
  output output5,
  output output10
);

  wire a, and_1_out, and_2_out, and_3_out, and_4_out, and_5_out, and_6_out, and_7_out, and_8_out, and_9_out,
       and_10_out, and_11_out, and_12_out, and_13_out, and_14_out, and_15_out, and_16_out, and_17_out,
       and_18_out, and_19_out, and_20_out, and_21_out, and_22_out, and_23_out, and_24_out, and_25_out,
       and_26_out, ap, b, bp, c, cp, na, nb, nc, nin1, nin2, nin3;

  not not_1 (nin1, input5);
  not not_2 (nin2, input10);
  not not_3 (nin3, input20);
  and and_1 (and_1_out, na, nb, input10);
  and and_2 (and_2_out, nb, nc, input10);
  and and_3 (and_3_out, nb, c, input5);
  and and_4 (and_4_out, na, b, nc, nin2);
  and and_5 (and_5_out, b, nin1, nin2, nin3);
  and and_6 (and_6_out, b, c, input20);
  and and_7 (and_7_out, a, input20);
  and and_8 (and_8_out, a, c, input10);
  and and_9 (and_9_out, a, b, input10);
  and and_10 (and_10_out, a, b, input5);
  D_Flip_Flop d_ff_1 (.D(ap), .clk(sysclock), .Q(a), .Qn(na));  // open: preset, reset
  D_Flip_Flop d_ff_2 (.D(bp), .clk(sysclock), .Q(b), .Qn(nb));  // open: preset, reset
  D_Flip_Flop d_ff_3 (.D(cp), .clk(sysclock), .Q(c), .Qn(nc));  // open: preset, reset
  or or_1 (bp, and_1_out, and_2_out, and_3_out, and_4_out, and_5_out);
  or or_2 (outputcoke, and_6_out, and_7_out, and_8_out, and_9_out, and_10_out);
  and and_11 (and_11_out, na, nb, input20);
  and and_12 (and_12_out, na, nc, input20);
  and and_13 (and_13_out, na, b, input10);
  and and_14 (and_14_out, b, c, input5);
  and and_15 (and_15_out, a, nc, nin3, nb);
  and and_16 (and_16_out, a, nin1, nin2, nin3);
  and and_17 (and_17_out, a, nb, input5);
  and and_18 (and_18_out, a, nc, input20);
  and and_19 (and_19_out, a, b, input10);
  and and_20 (and_20_out, a, c, input20);
  and and_21 (and_21_out, a, b, input20);
  and and_22 (and_22_out, na, nc, input5);
  and and_23 (and_23_out, nb, nc, input5);
  and and_24 (and_24_out, na, nb, c, nin1);
  and and_25 (and_25_out, c, nin1, nin2, nin3);
  and and_26 (and_26_out, na, c, input10);
  or or_3 (output10, and_20_out, and_21_out);
  or or_4 (ap, and_11_out, and_12_out, and_13_out, and_14_out, and_15_out, and_16_out, and_17_out);
  or or_5 (output5, and_18_out, and_19_out);
  or or_6 (cp, and_22_out, and_23_out, and_24_out, and_25_out, and_26_out);

  // Other names for the same wires on the sheet: clo = sysclock; f = outputcoke; in1 = input5; in2 = input10;
  //   in3 = input20; out1 = output5; out2 = output10
endmodule
