// Logisim project 3tester.circ as structural Verilog: 1 circuit, main circuit main
module main (
  output inputu,
  output sysclock,
  output outputn,
  output halt
);

  wire not_1_out;

  Clock clock_1 (.out(sysclock));
  Counter #(.width(9), .max('h1ff), .ongoal("stay")) counter_1 (
    .up(1'b1), .clk(sysclock), .carry(halt));  // open: clr, load, count, D, Q
  Random #(.width(1), .seed(666)) random_1 (.next(not_1_out), .clk(sysclock), .out(inputu));  // open: clr
  not not_1 (not_1_out, halt);
  fsmtable fsmtable_1 (.inputu(inputu), .sysclock(sysclock), .outputn(outputn));

  // Notes on the sheet:
  //   Place your subcircuit here.
endmodule
