// Logisim project 1.circ as structural Verilog: 2 circuits, main circuit alu8
module alu8 (
  input  [7:0] a,
  input  [7:0] b,
  input  [3:0] op,
  output [7:0] rddata
);

  wire cla_1_out_5, cla_3_out_5;
  wire [0:0] MUX1101;
  wire [3:0] Diff14, Diff58, not_2_out, not_3_out;
  wire [7:0] MUX0001, MUX0010, MUX0011, MUX0100, MUX0101, xnor_1_out;

  assign MUX0001 = ~a;  // NOT_Gate not_1, 8 bits wide
  and and_1 (MUX0010[0], a[0], b[0]);
  and and_2 (MUX0010[1], a[1], b[1]);
  and and_3 (MUX0010[2], a[2], b[2]);
  and and_4 (MUX0010[3], a[3], b[3]);
  and and_5 (MUX0010[4], a[4], b[4]);
  and and_6 (MUX0010[5], a[5], b[5]);
  CLA cla_1 (.in_1(a[3:0]), .in_2(b[3:0]), .in_3(1'b0), .out_4(MUX0101[3:0]), .out_5(cla_1_out_5));
  CLA cla_2 (.in_1(a[7:4]), .in_2(b[7:4]), .in_3(cla_1_out_5), .out_4(MUX0101[7:4]));  // open: out_5
  and and_7 (MUX0010[6], a[6], b[6]);
  and and_8 (MUX0010[7], a[7], b[7]);
  assign not_2_out = ~b[3:0];  // NOT_Gate not_2, 4 bits wide
  assign not_3_out = ~b[7:4];  // NOT_Gate not_3, 4 bits wide
  xor xor_1 (MUX0011[0], a[0], b[0]);
  xor xor_2 (MUX0011[1], a[1], b[1]);
  xor xor_3 (MUX0011[2], a[2], b[2]);
  xor xor_4 (MUX0011[3], a[3], b[3]);
  CLA cla_3 (.in_1(a[3:0]), .in_2(not_2_out), .in_3(1'b1), .out_4(Diff14), .out_5(cla_3_out_5));
  CLA cla_4 (.in_1(a[7:4]), .in_2(not_3_out), .in_3(cla_3_out_5), .out_4(Diff58));  // open: out_5
  xor xor_5 (MUX0011[4], a[4], b[4]);
  xor xor_6 (MUX0011[5], a[5], b[5]);
  xor xor_7 (MUX0011[6], a[6], b[6]);
  xor xor_8 (MUX0011[7], a[7], b[7]);
  or or_1 (MUX0100[0], a[0], b[0]);
  or or_2 (MUX0100[1], a[1], b[1]);
  Multiplexer #(.select(4), .width(8), .enable("false")) multiplexer_1 (
    .in1(MUX0001), .in2(MUX0010), .in3(MUX0011), .in4(MUX0100), .in5(MUX0101), .in6({Diff58, Diff14}),
    .in7(a), .in8(b), .in9(MUX0101), .in10({Diff58, Diff14}), .in11({a[6:0], 1'b0}), .in12({1'b0, a[7:1]}),
    .in13({{7{1'b0}}, MUX1101[0]}), .out(rddata), .sel(op));  // open: in0, in14, in15
  or or_3 (MUX0100[2], a[2], b[2]);
  or or_4 (MUX0100[3], a[3], b[3]);
  or or_5 (MUX0100[4], a[4], b[4]);
  or or_6 (MUX0100[5], a[5], b[5]);
  or or_7 (MUX0100[6], a[6], b[6]);
  or or_8 (MUX0100[7], a[7], b[7]);
  assign xnor_1_out = ~(a ^ b);  // XNOR_Gate xnor_1, 8 bits wide
  and and_9 (MUX1101[0], xnor_1_out[0], xnor_1_out[1], xnor_1_out[2], xnor_1_out[3], xnor_1_out[4], xnor_1_out[5], xnor_1_out[6], xnor_1_out[7]);

  // Other names for the same wires on the sheet: B1 = b[0]; B14[3:0] = b[3:0]; MUX1000[7:0] = b; B2 = b[1]; B3 = b[2];
  //   B4 = b[3]; B5 = b[4]; B58[3:0] = b[7:4]; B6 = b[5]; B7 = b[6]; B8 = b[7]; MUX1001[7:0] = MUX0101;
  //   sum14[3:0] = MUX0101[3:0]; sum58[3:0] = MUX0101[7:4]; MUX0110[7:0] = {Diff58, Diff14};
  //   MUX1010[7:0] = {Diff58, Diff14}; A1 = a[0]; A14[3:0] = a[3:0]; MUX0111[7:0] = a; MUX1011[7:1] = a[6:0];
  //   A2 = a[1]; MUX1100[6:0] = a[7:1]; A3 = a[2]; A4 = a[3]; A5 = a[4]; A58[3:0] = a[7:4]; A6 = a[5]; A7 = a[6];
  //   A8 = a[7]; opcode[3:0] = op
endmodule

module CLA (
  input  [3:0] in_1,
  input  [3:0] in_2,
  input  in_3,
  output [3:0] out_4,
  output out_5
);

  wire and_2_out, and_4_out, and_5_out, and_7_out, and_8_out, and_9_out, and_11_out, and_12_out, and_13_out,
       and_14_out;
  wire [2:0] C;
  wire [3:0] G, P;

  and and_1 (G[0], in_1[0], in_2[0]);
  and and_2 (and_2_out, in_3, P[0]);
  xor xor_1 (out_4[0], P[0], in_3);
  or or_1 (C[0], G[0], and_2_out);
  xor xor_2 (P[0], in_1[0], in_2[0]);
  and and_3 (G[1], in_1[1], in_2[1]);
  and and_4 (and_4_out, P[1], G[0]);
  and and_5 (and_5_out, P[1], P[0], in_3);
  xor xor_3 (out_4[1], P[1], C[0]);
  xor xor_4 (P[1], in_1[1], in_2[1]);
  or or_2 (C[1], G[1], and_4_out, and_5_out);
  and and_6 (G[2], in_1[2], in_2[2]);
  xor xor_5 (P[2], in_1[2], in_2[2]);
  and and_7 (and_7_out, P[2], G[1]);
  and and_8 (and_8_out, P[2], P[1], G[0]);
  and and_9 (and_9_out, P[2], P[1], P[0], in_3);
  and and_10 (G[3], in_1[3], in_2[3]);
  or or_3 (C[2], G[2], and_7_out, and_8_out, and_9_out);
  xor xor_6 (out_4[2], P[2], C[1]);
  xor xor_7 (P[3], in_1[3], in_2[3]);
  and and_11 (and_11_out, P[3], G[2]);
  and and_12 (and_12_out, P[3], P[2], G[1]);
  and and_13 (and_13_out, P[3], P[2], P[1], G[0]);
  and and_14 (and_14_out, P[3], P[2], P[1], P[0], in_3);
  xor xor_8 (out_4[3], P[3], C[2]);
  or or_4 (out_5, G[3], and_11_out, and_12_out, and_13_out, and_14_out);

  // Other names for the same wires on the sheet: A[3:0] = in_1; B[3:0] = in_2; C1 = C[0]; C2 = C[1]; C3 = C[2];
  //   C[3] = out_5; C4 = out_5; C0 = in_3; O[3:0] = out_4; O1 = out_4[0]; O2 = out_4[1]; O3 = out_4[2]; O4 = out_4[3]
endmodule
