// Logisim project 3.circ as structural Verilog: 1 circuit, main circuit regfile
module regfile (
  input  [2:0] rd,
  input  [7:0] rddata,
  input  wen,
  input  resetall,
  input  sysclock,
  output [7:0] x0,
  output [7:0] x1,
  output [7:0] x2,
  output [7:0] x3,
  output [7:0] x4,
  output [7:0] x5,
  output [7:0] x6,
  output [7:0] x7
);

  wire and_1_out, and_2_out, and_3_out, and_4_out, and_5_out, and_6_out, and_7_out, and_8_out,
       decoder_1_out0, decoder_1_out1, decoder_1_out2, decoder_1_out3, decoder_1_out4, decoder_1_out5,
       decoder_1_out6, decoder_1_out7;

  Decoder #(.select(3)) decoder_1 (
    .out0(decoder_1_out0), .out1(decoder_1_out1), .out2(decoder_1_out2), .out3(decoder_1_out3),
    .out4(decoder_1_out4), .out5(decoder_1_out5), .out6(decoder_1_out6), .out7(decoder_1_out7), .sel(rd));  // open: en
  and and_1 (and_1_out, decoder_1_out0, wen);
  and and_2 (and_2_out, decoder_1_out1, wen);
  and and_3 (and_3_out, decoder_1_out2, wen);
  and and_4 (and_4_out, decoder_1_out3, wen);
  and and_5 (and_5_out, decoder_1_out4, wen);
  and and_6 (and_6_out, decoder_1_out5, wen);
  and and_7 (and_7_out, decoder_1_out6, wen);
  and and_8 (and_8_out, decoder_1_out7, wen);
  Register register_1 (.D(rddata), .en(and_1_out), .clk(sysclock), .Q(x0), .clr(resetall));
  Register register_2 (.D(rddata), .en(and_2_out), .clk(sysclock), .Q(x1), .clr(resetall));
  Register register_3 (.D(rddata), .en(and_3_out), .clk(sysclock), .Q(x2), .clr(resetall));
  Register register_4 (.D(rddata), .en(and_4_out), .clk(sysclock), .Q(x3), .clr(resetall));
  Register register_5 (.D(rddata), .en(and_5_out), .clk(sysclock), .Q(x4), .clr(resetall));
  Register register_6 (.D(rddata), .en(and_6_out), .clk(sysclock), .Q(x5), .clr(resetall));
  Register register_7 (.D(rddata), .en(and_7_out), .clk(sysclock), .Q(x6), .clr(resetall));
  Register register_8 (.D(rddata), .en(and_8_out), .clk(sysclock), .Q(x7), .clr(resetall));

  // Other names for the same wires on the sheet: a[2:0] = rd; b[7:0] = rddata; c = wen; clo = sysclock; d = resetall;
  //   xx1[7:0] = x0; xx2[7:0] = x1; xx3[7:0] = x2; xx4[7:0] = x3; xx5[7:0] = x4; xx6[7:0] = x5; xx7[7:0] = x6;
  //   xx8[7:0] = x7
endmodule
