// Logisim project 4.circ as structural Verilog: 5 circuits, main circuit cpu
module cpu (
  input  resetall,
  input  sysclock,
  output [7:0] pc,
  output [7:0] x0,
  output [7:0] x1,
  output [7:0] x2,
  output [7:0] x3,
  output [7:0] x4,
  output [7:0] x5,
  output [7:0] x6,
  output [7:0] x7
);

  wire a, and_3_out, and_4_out, and_5_out, and_6_out, and_7_out, and_8_out, and_9_out, b, c, cho1, cho2, clo,
       d, halt, not_1_out, not_2_out, not_3_out, not_4_out, not_5_out, not_6_out, not_7_out, not_8_out,
       not_9_out, not_10_out, sel, stop, wen, wenwen;
  wire [2:0] destinition, rs1, rs2;
  wire [7:0] imm, multiplexer_1_out, multiplexer_2_out, multiplexer_3_out, rddata;

  Multiplexer #(.select(3), .width(8), .enable("false")) multiplexer_1 (
    .in0(x0), .in1(x1), .in2(x2), .in3(x3), .in4(x4), .in5(x5), .in6(x6), .in7(x7), .out(multiplexer_1_out),
    .sel(rs1));
  D_Flip_Flop d_ff_1 (.Qn(cho1), .preset(halt), .reset(resetall));  // open: D, clk, Q
  D_Flip_Flop d_ff_2 (.Qn(cho2), .preset(stop));  // open: D, clk, Q, reset
  Multiplexer #(.select(3), .width(8), .enable("false")) multiplexer_2 (
    .in0(x0), .in1(x1), .in2(x2), .in3(x3), .in4(x4), .in5(x5), .in6(x6), .in7(x7), .out(multiplexer_2_out),
    .sel(rs2));
  Multiplexer #(.width(8), .enable("false")) multiplexer_3 (
    .in0(multiplexer_2_out), .in1(imm), .out(multiplexer_3_out), .sel(sel));
  and and_1 (clo, sysclock, cho2);
  and and_2 (wenwen, wen, cho1, cho2);
  not not_1 (not_1_out, b);
  not not_2 (not_2_out, c);
  not not_3 (not_3_out, b);
  not not_4 (not_4_out, d);
  alu8 alu8_1 (.a(multiplexer_1_out), .b(multiplexer_3_out), .op({a, b, c, d}), .rddata(rddata));
  and and_3 (and_3_out, a, not_1_out, not_2_out);
  and and_4 (and_4_out, a, not_3_out, not_4_out);
  not not_5 (not_5_out, a);
  not not_6 (not_6_out, a);
  not not_7 (not_7_out, a);
  not not_8 (not_8_out, b);
  not not_9 (not_9_out, c);
  or or_1 (sel, and_3_out, and_4_out);
  and and_5 (and_5_out, not_5_out, d);
  and and_6 (and_6_out, not_6_out, c);
  and and_7 (and_7_out, not_7_out, b);
  and and_8 (and_8_out, not_8_out, a);
  and and_9 (and_9_out, not_9_out, a);
  instructions instructions_1 (
    .resetall(resetall), .sysclock(clo), .pc(pc), .op({a, b, c, d}), .rd(destinition), .rs1(rs1), .rs2(rs2),
    .imm(imm));
  or or_2 (wen, and_5_out, and_6_out, and_7_out, and_8_out, and_9_out);
  regfile regfile_1 (
    .rd(destinition), .rddata(rddata), .wen(wenwen), .resetall(resetall), .sysclock(clo), .x0(x0), .x1(x1),
    .x2(x2), .x3(x3), .x4(x4), .x5(x5), .x6(x6), .x7(x7));
  not not_10 (not_10_out, d);
  and and_10 (halt, a, b, c, not_10_out);
  and and_11 (stop, a, b, c, d);

  // Other names for the same wires on the sheet: opcode[3:0] = {a, b, c, d}; reset = resetall
endmodule

module alu8 (
  input  [7:0] a,
  input  [7:0] b,
  input  [3:0] op,
  output [7:0] rddata
);

  wire cla_1_out_5, cla_3_out_5;
  wire [0:0] MUX1101;
  wire [3:0] Diff14, Diff58, not_2_out, not_3_out;
  wire [7:0] MUX0001, MUX0010, MUX0011, MUX0100, MUX0101, xnor_1_out;

  assign MUX0001 = ~a;  // NOT_Gate not_1, 8 bits wide
  and and_1 (MUX0010[0], a[0], b[0]);
  and and_2 (MUX0010[2], a[2], b[2]);
  and and_3 (MUX0010[1], a[1], b[1]);
  and and_4 (MUX0010[3], a[3], b[3]);
  and and_5 (MUX0010[4], a[4], b[4]);
  and and_6 (MUX0010[5], a[5], b[5]);
  CLA cla_1 (.in_1(a[3:0]), .in_2(b[3:0]), .in_3(1'b0), .out_4(MUX0101[3:0]), .out_5(cla_1_out_5));
  CLA cla_2 (.in_1(a[7:4]), .in_2(b[7:4]), .in_3(cla_1_out_5), .out_4(MUX0101[7:4]));  // open: out_5
  and and_7 (MUX0010[6], a[6], b[6]);
  and and_8 (MUX0010[7], a[7], b[7]);
  assign not_2_out = ~b[3:0];  // NOT_Gate not_2, 4 bits wide
  assign not_3_out = ~b[7:4];  // NOT_Gate not_3, 4 bits wide
  xor xor_1 (MUX0011[0], a[0], b[0]);
  xor xor_2 (MUX0011[2], a[2], b[2]);
  xor xor_3 (MUX0011[1], a[1], b[1]);
  xor xor_4 (MUX0011[3], a[3], b[3]);
  CLA cla_3 (.in_1(a[3:0]), .in_2(not_2_out), .in_3(1'b1), .out_4(Diff14), .out_5(cla_3_out_5));
  CLA cla_4 (.in_1(a[7:4]), .in_2(not_3_out), .in_3(cla_3_out_5), .out_4(Diff58));  // open: out_5
  xor xor_5 (MUX0011[4], a[4], b[4]);
  xor xor_6 (MUX0011[5], a[5], b[5]);
  xor xor_7 (MUX0011[6], a[6], b[6]);
  xor xor_8 (MUX0011[7], a[7], b[7]);
  or or_1 (MUX0100[0], a[0], b[0]);
  or or_2 (MUX0100[1], a[1], b[1]);
  Multiplexer #(.select(4), .width(8), .enable("false")) multiplexer_1 (
    .in1(MUX0001), .in2(MUX0010), .in3(MUX0011), .in4(MUX0100), .in5(MUX0101), .in6({Diff58, Diff14}),
    .in7(a), .in8(b), .in9(MUX0101), .in10({Diff58, Diff14}), .in11({a[6:0], 1'b0}), .in12({1'b0, a[7:1]}),
    .in13({{7{1'b0}}, MUX1101[0]}), .out(rddata), .sel(op));  // open: in0, in14, in15
  or or_3 (MUX0100[2], a[2], b[2]);
  or or_4 (MUX0100[3], a[3], b[3]);
  or or_5 (MUX0100[4], a[4], b[4]);
  or or_6 (MUX0100[5], a[5], b[5]);
  or or_7 (MUX0100[6], a[6], b[6]);
  or or_8 (MUX0100[7], a[7], b[7]);
  assign xnor_1_out = ~(a ^ b);  // XNOR_Gate xnor_1, 8 bits wide
  and and_9 (MUX1101[0], xnor_1_out[0], xnor_1_out[1], xnor_1_out[2], xnor_1_out[3], xnor_1_out[4], xnor_1_out[5], xnor_1_out[6], xnor_1_out[7]);

  // Other names for the same wires on the sheet: B1 = b[0]; B14[3:0] = b[3:0]; MUX1000[7:0] = b; B2 = b[1]; B3 = b[2];
  //   B4 = b[3]; B5 = b[4]; B58[3:0] = b[7:4]; B6 = b[5]; B7 = b[6]; B8 = b[7]; MUX1001[7:0] = MUX0101;
  //   sum14[3:0] = MUX0101[3:0]; sum58[3:0] = MUX0101[7:4]; MUX0110[7:0] = {Diff58, Diff14};
  //   MUX1010[7:0] = {Diff58, Diff14}; A1 = a[0]; A14[3:0] = a[3:0]; MUX0111[7:0] = a; MUX1011[7:1] = a[6:0];
  //   A2 = a[1]; MUX1100[6:0] = a[7:1]; A3 = a[2]; A4 = a[3]; A5 = a[4]; A58[3:0] = a[7:4]; A6 = a[5]; A7 = a[6];
  //   A8 = a[7]; opcode[3:0] = op
endmodule

module CLA (
  input  [3:0] in_1,
  input  [3:0] in_2,
  input  in_3,
  output [3:0] out_4,
  output out_5
);

  wire and_2_out, and_4_out, and_5_out, and_7_out, and_8_out, and_9_out, and_11_out, and_12_out, and_13_out,
       and_14_out;
  wire [2:0] C;
  wire [3:0] G, P;

  and and_1 (G[0], in_1[0], in_2[0]);
  and and_2 (and_2_out, in_3, P[0]);
  xor xor_1 (out_4[0], P[0], in_3);
  or or_1 (C[0], G[0], and_2_out);
  xor xor_2 (P[0], in_1[0], in_2[0]);
  and and_3 (G[1], in_1[1], in_2[1]);
  and and_4 (and_4_out, P[1], G[0]);
  and and_5 (and_5_out, P[1], P[0], in_3);
  xor xor_3 (out_4[1], P[1], C[0]);
  xor xor_4 (P[1], in_1[1], in_2[1]);
  or or_2 (C[1], G[1], and_4_out, and_5_out);
  and and_6 (G[2], in_1[2], in_2[2]);
  xor xor_5 (P[2], in_1[2], in_2[2]);
  and and_7 (and_7_out, P[2], G[1]);
  and and_8 (and_8_out, P[2], P[1], G[0]);
  and and_9 (and_9_out, P[2], P[1], P[0], in_3);
  and and_10 (G[3], in_1[3], in_2[3]);
  or or_3 (C[2], G[2], and_7_out, and_8_out, and_9_out);
  xor xor_6 (out_4[2], P[2], C[1]);
  xor xor_7 (P[3], in_1[3], in_2[3]);
  and and_11 (and_11_out, P[3], G[2]);
  and and_12 (and_12_out, P[3], P[2], G[1]);
  and and_13 (and_13_out, P[3], P[2], P[1], G[0]);
  and and_14 (and_14_out, P[3], P[2], P[1], P[0], in_3);
  xor xor_8 (out_4[3], P[3], C[2]);
  or or_4 (out_5, G[3], and_11_out, and_12_out, and_13_out, and_14_out);

  // Other names for the same wires on the sheet: A[3:0] = in_1; B[3:0] = in_2; C1 = C[0]; C2 = C[1]; C3 = C[2];
  //   C[3] = out_5; C4 = out_5; C0 = in_3; O[3:0] = out_4; O1 = out_4[0]; O2 = out_4[1]; O3 = out_4[2]; O4 = out_4[3]
endmodule

module instructions (
  input  resetall,
  input  sysclock,
  output [7:0] pc,
  output [3:0] op,
  output [2:0] rd,
  output [2:0] rs1,
  output [2:0] rs2,
  output [7:0] imm
);

  Counter counter_1 (.clr(resetall), .clk(sysclock), .Q(pc));  // open: load, up, count, D, carry
  RAM #(.dataWidth(21)) ram_1 (.addr(pc), .we(1'b0), .oe(1'b1), .clk(sysclock), .data({op, rd, rs1, rs2, imm}));

  // Other names for the same wires on the sheet: clock = sysclock; reset = resetall
endmodule

module regfile (
  input  [2:0] rd,
  input  [7:0] rddata,
  input  wen,
  input  resetall,
  input  sysclock,
  output [7:0] x0,
  output [7:0] x1,
  output [7:0] x2,
  output [7:0] x3,
  output [7:0] x4,
  output [7:0] x5,
  output [7:0] x6,
  output [7:0] x7
);

  wire and_1_out, and_2_out, and_3_out, and_4_out, and_5_out, and_6_out, and_7_out, and_8_out,
       decoder_1_out0, decoder_1_out1, decoder_1_out2, decoder_1_out3, decoder_1_out4, decoder_1_out5,
       decoder_1_out6, decoder_1_out7;

  Decoder #(.select(3)) decoder_1 (
    .out0(decoder_1_out0), .out1(decoder_1_out1), .out2(decoder_1_out2), .out3(decoder_1_out3),
    .out4(decoder_1_out4), .out5(decoder_1_out5), .out6(decoder_1_out6), .out7(decoder_1_out7), .sel(rd));  // open: en
  and and_1 (and_1_out, decoder_1_out0, wen);
  and and_2 (and_2_out, decoder_1_out1, wen);
  and and_3 (and_3_out, decoder_1_out2, wen);
  and and_4 (and_4_out, decoder_1_out3, wen);
  and and_5 (and_5_out, decoder_1_out4, wen);
  and and_6 (and_6_out, decoder_1_out5, wen);
  and and_7 (and_7_out, decoder_1_out6, wen);
  and and_8 (and_8_out, decoder_1_out7, wen);
  Register register_1 (.D(rddata), .en(and_1_out), .clk(sysclock), .Q(x0), .clr(resetall));
  Register register_2 (.D(rddata), .en(and_2_out), .clk(sysclock), .Q(x1), .clr(resetall));
  Register register_3 (.D(rddata), .en(and_3_out), .clk(sysclock), .Q(x2), .clr(resetall));
  Register register_4 (.D(rddata), .en(and_4_out), .clk(sysclock), .Q(x3), .clr(resetall));
  Register register_5 (.D(rddata), .en(and_5_out), .clk(sysclock), .Q(x4), .clr(resetall));
  Register register_6 (.D(rddata), .en(and_6_out), .clk(sysclock), .Q(x5), .clr(resetall));
  Register register_7 (.D(rddata), .en(and_7_out), .clk(sysclock), .Q(x6), .clr(resetall));
  Register register_8 (.D(rddata), .en(and_8_out), .clk(sysclock), .Q(x7), .clr(resetall));

  // Other names for the same wires on the sheet: a[2:0] = rd; b[7:0] = rddata; c = wen; clo = sysclock; d = resetall;
  //   xx1[7:0] = x0; xx2[7:0] = x1; xx3[7:0] = x2; xx4[7:0] = x3; xx5[7:0] = x4; xx6[7:0] = x5; xx7[7:0] = x6;
  //   xx8[7:0] = x7
endmodule
